// Digital circuit 8 x 1 MUX.dig as structural Verilog
module _8_x_1_MUX (
  input  X,
  input  Y,
  input  Z,
  input  I0,
  input  I1,
  input  I2,
  input  I3,
  input  I4,
  input  I5,
  input  I6,
  input  I7,
  output out
);

  wire and_1_out, and_2_out, and_3_out, and_4_out, and_5_out, and_6_out, and_7_out, and_8_out, not_1_out,
       not_2_out, not_3_out;

  not not_1 (not_1_out, X);
  not not_2 (not_2_out, Y);
  not not_3 (not_3_out, Z);
  and and_1 (and_1_out, not_1_out, not_2_out, not_3_out, I0);
  and and_2 (and_2_out, not_1_out, not_2_out, Z, I1);
  and and_3 (and_3_out, not_1_out, Y, not_3_out, I2);
  and and_4 (and_4_out, Y, Z, not_1_out, I3);
  and and_5 (and_5_out, X, not_2_out, not_3_out, I4);
  and and_6 (and_6_out, X, Z, not_2_out, I5);
  and and_7 (and_7_out, X, Y, not_3_out, I6);
  and and_8 (and_8_out, X, Y, Z, I7);
  or or_1 (out, and_1_out, and_2_out, and_3_out, and_4_out, and_5_out, and_6_out, and_7_out, and_8_out);
endmodule
