// Digital circuit ALU_4bit.dig as structural Verilog
module ALU_4bit (
  input  A3,
  input  A2,
  input  A1,
  input  A0,
  input  B3,
  input  B2,
  input  B1,
  input  B0,
  input  S2,
  input  S1,
  input  S0
);

  wire add_sub_1_su0, add_sub_1_su1, add_sub_1_su2, add_sub_1_su3, left_shift_1_sl0, left_shift_1_sl1,
       left_shift_1_sl2, left_shift_1_sl3, logic_part_1_an0, logic_part_1_an1, logic_part_1_an2,
       logic_part_1_an3, logic_part_1_not0, logic_part_1_not1, logic_part_1_not2, logic_part_1_not3,
       logic_part_1_or0, logic_part_1_or1, logic_part_1_or2, logic_part_1_or3, logic_part_1_xor0,
       logic_part_1_xor1, logic_part_1_xor2, logic_part_1_xor3, right_shift_1_sr0, right_shift_1_sr1,
       right_shift_1_sr2, right_shift_1_sr3, subtractor_1_sub0, subtractor_1_sub1, subtractor_1_sub2,
       subtractor_1_sub3;
  wire [0:0] add_sub_1_c;
  wire [3:0] _8_x_1_mux_1_out;

  Add_Sub add_sub_1 (
    .A0(A0), .B0(B0), .S0(S0), .A1(A1), .A2(A2), .A3(A3), .B1(B1), .B2(B2), .B3(B3), .C(add_sub_1_c[0]),
    .su3(add_sub_1_su3), .su0(add_sub_1_su0), .su1(add_sub_1_su1), .su2(add_sub_1_su2));  // open: _0
  logic_part logic_part_1 (
    .A0(A0), .B0(B0), .A1(A1), .A2(A2), .A3(A3), .B1(B1), .B2(B2), .B3(B3), .an0(logic_part_1_an0),
    .an1(logic_part_1_an1), .an2(logic_part_1_an2), .an3(logic_part_1_an3), .or0(logic_part_1_or0),
    .or1(logic_part_1_or1), .or2(logic_part_1_or2), .or3(logic_part_1_or3), .xor0(logic_part_1_xor0),
    .xor1(logic_part_1_xor1), .xor2(logic_part_1_xor2), .xor3(logic_part_1_xor3), .not0(logic_part_1_not0),
    .not1(logic_part_1_not1), .not2(logic_part_1_not2), .not3(logic_part_1_not3));
  left_shift left_shift_1 (
    .A0(A0), .A1(A1), .A2(A2), .SL3(left_shift_1_sl3), .SL2(left_shift_1_sl2), .SL1(left_shift_1_sl1),
    .SL0(left_shift_1_sl0));
  right_shift right_shift_1 (
    .A1(A1), .A2(A2), .A3(A3), .SR2(right_shift_1_sr2), .SR1(right_shift_1_sr1), .SR0(right_shift_1_sr0),
    .SR3(right_shift_1_sr3));
  subtractor subtractor_1 (
    .B3(B3), .B2(B2), .B1(B1), .B0(B0), .A0(A0), .A1(A1), .A2(A2), .A3(A3), .sub0(subtractor_1_sub0),
    .sub1(subtractor_1_sub1), .sub2(subtractor_1_sub2), .sub3(subtractor_1_sub3));  // open: B
  _8_x_1_MUX _8_x_1_mux_1 (
    .X(S2), .Y(S1), .Z(S0), .I0(add_sub_1_su0), .I1(logic_part_1_an0), .I2(logic_part_1_or0),
    .I3(logic_part_1_xor0), .I4(logic_part_1_not0), .I5(left_shift_1_sl0), .I6(right_shift_1_sr0),
    .I7(subtractor_1_sub0), .out(_8_x_1_mux_1_out[0]));
  _8_x_1_MUX _8_x_1_mux_2 (
    .X(S2), .Y(S1), .Z(S0), .I0(add_sub_1_su1), .I1(logic_part_1_an1), .I2(logic_part_1_or1),
    .I3(logic_part_1_xor1), .I4(logic_part_1_not1), .I5(left_shift_1_sl1), .I6(right_shift_1_sr1),
    .I7(subtractor_1_sub1), .out(_8_x_1_mux_1_out[1]));
  _8_x_1_MUX _8_x_1_mux_3 (
    .X(S2), .Y(S1), .Z(S0), .I0(add_sub_1_su2), .I1(logic_part_1_an2), .I2(logic_part_1_or2),
    .I3(logic_part_1_xor2), .I4(logic_part_1_not2), .I5(left_shift_1_sl2), .I6(right_shift_1_sr2),
    .I7(subtractor_1_sub2), .out(_8_x_1_mux_1_out[2]));
  _8_x_1_MUX _8_x_1_mux_4 (
    .X(S2), .Y(S1), .Z(S0), .I0(add_sub_1_su3), .I1(logic_part_1_an3), .I2(logic_part_1_or3),
    .I3(logic_part_1_xor3), .I4(logic_part_1_not3), .I5(left_shift_1_sl3), .I6(right_shift_1_sr3),
    .I7(subtractor_1_sub3), .out(_8_x_1_mux_1_out[3]));
  LED led_1 (.in(add_sub_1_c[0]));
  LED led_2 (.in(_8_x_1_mux_1_out[3]));
  Seven_Seg_Hex seven_seg_hex_1 (.d({3'b000, add_sub_1_c[0]}), .dp(1'b0));
  LED led_3 (.in(_8_x_1_mux_1_out[1]));
  LED led_4 (.in(_8_x_1_mux_1_out[2]));
  Seven_Seg_Hex seven_seg_hex_2 (.d(_8_x_1_mux_1_out), .dp(1'b0));
  LED LSB (.in(_8_x_1_mux_1_out[0]));
endmodule
