// Digital circuit Add_Sub.dig as structural Verilog
module Add_Sub (
  input  A0,
  input  B0,
  input  S0,
  input  A1,
  input  A2,
  input  A3,
  input  B1,
  input  B2,
  input  B3,
  output C,
  output _0,
  output su3,
  output su0,
  output su1,
  output su2
);

  wire or_1_out, or_2_out, or_3_out;

  Binary_Adder_Subtractor binary_adder_subtractor_1 (
    .M(S0), .B0(B0), .B1(B1), .B2(B2), .B3(B3), .A0(A0), .A1(A1), .A2(A2), .A3(A3), .Cout(C), .S0(su0),
    .S1(su1), .S2(su2), .S3(su3));
  or or_1 (or_1_out, su0, su1);
  or or_2 (or_2_out, su2, su3);
  or or_3 (or_3_out, or_1_out, or_2_out);
  not not_1 (_0, or_3_out);
endmodule
