// Digital circuit Binary Adder Subtractor.dig as structural Verilog
module Binary_Adder_Subtractor (
  input  M,
  input  B0,
  input  B1,
  input  B2,
  input  B3,
  input  A0,
  input  A1,
  input  A2,
  input  A3,
  output Cout,
  output S0,
  output S1,
  output S2,
  output S3
);

  wire full_adder_2_co, full_adder_3_co, full_adder_4_co, xor_1_out, xor_2_out, xor_3_out, xor_4_out;

  xor xor_1 (xor_1_out, M, B3);
  Full_Adder full_adder_1 (.A(A3), .B(xor_1_out), .Ci(full_adder_2_co), .S(S3), .Co(Cout));
  xor xor_2 (xor_2_out, M, B2);
  Full_Adder full_adder_2 (.A(A2), .B(xor_2_out), .Ci(full_adder_3_co), .S(S2), .Co(full_adder_2_co));
  xor xor_3 (xor_3_out, M, B1);
  Full_Adder full_adder_3 (.A(A1), .B(xor_3_out), .Ci(full_adder_4_co), .S(S1), .Co(full_adder_3_co));
  xor xor_4 (xor_4_out, M, B0);
  Full_Adder full_adder_4 (.A(A0), .B(xor_4_out), .Ci(M), .S(S0), .Co(full_adder_4_co));
endmodule
