// Digital circuit Full Adder.dig as structural Verilog
module Full_Adder (
  input  A,
  input  B,
  input  Ci,
  output S,
  output Co
);

  wire half_adder_1_co, half_adder_1_s, half_adder_2_co;

  Half_Adder half_adder_1 (.x(A), .y(B), .S(half_adder_1_s), .Co(half_adder_1_co));
  Half_Adder half_adder_2 (.x(half_adder_1_s), .y(Ci), .S(S), .Co(half_adder_2_co));
  or or_1 (Co, half_adder_2_co, half_adder_1_co);
endmodule
