// Digital circuit half subtractor.dig as structural Verilog
module half_subtractor (
  input  B,
  input  A,
  output Diff,
  output Bor
);

  wire not_1_out;

  not not_1 (not_1_out, B);
  xor xor_1 (Diff, B, A);
  and and_1 (Bor, not_1_out, A);
endmodule
