// Digital circuit logic_part.dig as structural Verilog
module logic_part (
  input  A0,
  input  B0,
  input  A1,
  input  A2,
  input  A3,
  input  B1,
  input  B2,
  input  B3,
  output an0,
  output an1,
  output an2,
  output an3,
  output or0,
  output or1,
  output or2,
  output or3,
  output xor0,
  output xor1,
  output xor2,
  output xor3,
  output not0,
  output not1,
  output not2,
  output not3
);

  and and_1 (an0, A0, B0);
  and and_2 (an1, A1, B1);
  and and_3 (an2, A2, B2);
  and and_4 (an3, A3, B3);
  or or_1 (or0, A0, B0);
  or or_2 (or1, A1, B1);
  or or_3 (or2, A2, B2);
  or or_4 (or3, A3, B3);
  xor xor_1 (xor0, A0, B0);
  xor xor_2 (xor1, A1, B1);
  xor xor_3 (xor2, A2, B2);
  xor xor_4 (xor3, A3, B3);
  not not_1 (not0, A0);
  not not_2 (not1, A1);
  not not_3 (not2, A2);
  not not_4 (not3, A3);
endmodule
