// Digital circuit subtractor.dig as structural Verilog
module subtractor (
  input  B3,
  input  B2,
  input  B1,
  input  B0,
  input  A0,
  input  A1,
  input  A2,
  input  A3,
  output B,
  output sub0,
  output sub1,
  output sub2,
  output sub3
);

  wire full_adder_2_co, full_adder_3_co, full_adder_4_co, not_1_out, not_2_out, not_3_out, not_4_out;

  Full_Adder full_adder_1 (.A(A3), .B(not_1_out), .Ci(full_adder_2_co), .S(sub3), .Co(B));
  not not_1 (not_1_out, B3);
  not not_2 (not_2_out, B2);
  Full_Adder full_adder_2 (.A(A2), .B(not_2_out), .Ci(full_adder_3_co), .S(sub2), .Co(full_adder_2_co));
  not not_3 (not_3_out, B1);
  Full_Adder full_adder_3 (.A(A1), .B(not_3_out), .Ci(full_adder_4_co), .S(sub1), .Co(full_adder_3_co));
  not not_4 (not_4_out, B0);
  Full_Adder full_adder_4 (.A(A0), .B(not_4_out), .Ci(1'b1), .S(sub0), .Co(full_adder_4_co));
endmodule
